# Fritzing sketch light_seeker_basic_prog (saved by Fritzing 0.8.7b)
breadboards: 1

parts:
  IC1 = L293D [package=THT]
  IC2 = IC, DIP package, 20 pins [chip_label=MSP430G2452 part_number=msp430g2452]
  J1 = male pin header, 5 pins [form="♂ (male)"]
  R1 = Resistor [tolerance=±5% resistance=47k package=THT]
  VCC1 = 4 x AAA Battery Mount
  C1 = Electrolytic Capacitor [capacitance=0.1mF voltage=16V package="100 mil [THT, electrolytic]"]
  J2 = male pin header, 2 pins [form="♂ (male)"]
  C2 = Ceramic Capacitor [capacitance=100nF voltage=50V package="100 mil [THT, multilayer]"]
  C3 = Ceramic Capacitor [capacitance=100nF voltage=50V package="100 mil [THT, multilayer]"]
  C4 = Electrolytic Capacitor [capacitance=0.1mF voltage=16V package="100 mil [THT, electrolytic]"]
  U1 = mystery part, 3 pins [chip_label=lp2950-33]
  J3 = male pin header, 2 pins [form="♂ (male)"]
  M1 = DC Motor
  M2 = DC Motor
  C5 = Electrolytic Capacitor [capacitance=47µF voltage=10V package="100 mil [THT, electrolytic]"]
  C6 = Electrolytic Capacitor [capacitance=47µF voltage=10V package="100 mil [THT, electrolytic]"]
  R2 = Resistor [tolerance=±5% resistance=33k package=THT]
  R3 = Resistor [tolerance=±5% resistance=33k package=THT]
  R4 = Photocell (LDR) [package=THT]
  R5 = Photocell (LDR) [package=THT]
  Launchpad1 = TI Launchpad MSP430G2

nets:
  N1: IC1.Enable_1, IC1.+Vmotor, IC1.Enable_2, IC1.+V, C1.+, J2.pin2, C4.+
  N2: IC1.In_1, IC2.pin5
  N3: IC1.Out_1_(_Controlled_by_Enable_1_), C2.0, M1.pin_2
  N4: IC1.0V, IC2.pin20, J1.pin5, VCC1.-, C1.-, C4.-, U1.pin2, C5.-, C6.-, R2.Pin_1, R3.Pin_0, Launchpad1.p20
  N5: IC1.Out_2_(_Controlled_by_Enable_1_), C2.1, M1.pin_1
  N6: IC1.In_2, IC2.pin6
  N7: IC1.In_3, IC2.pin14
  N8: IC1.Out_3_(_Controlled_by_Enable_2_), C3.0, M2.pin_2
  N9: IC1.Out_4_(_Controlled_by_Enable_2_), C3.1, M2.pin_1
  N10: IC1.In_4, IC2.pin15
  N11: IC2.pin1, J1.pin3, R1.Pin_1, U1.pin1, C5.+, R4.pin_0, R5.pin_1
  N12: IC2.pin2, R2.Pin_0, R4.pin_1
  N13: IC2.pin3, R3.Pin_1, R5.pin_0
  N14: IC2.pin16, J1.pin2, R1.Pin_0
  N15: IC2.pin17, J1.pin1
  N16: VCC1.+, J2.pin1, J3.pin1
  N17: U1.pin3, J3.pin2, C6.+

notes:
  this jumper is for the batteries to the 3.3V regulator which then goes to the msp430g2452.
  this jumper is to ------> connect the battery power to the L293D motor driver and the supply for the motors.
  Right motor
  Left Motor
  Left LDR/Photoresistor
  Right LDR/Photoresistor
